# Fritzing sketch rgb (saved by Fritzing 0.9.3b)
breadboards: 1

parts:
  Raspberry_Pi_1 = Raspberry Pi 3 [part_number=RPI-3-V1.2]
  S1 = Pushbutton [package="[THT]"]
  R1 = Resistor [tolerance=±5% resistance=10k package=THT]
  LED1 = RGB LED (com. cathode, rgb) [package="5 mm [THT]"]
  R2 = Resistor [tolerance=±5% resistance=220 package=THT]
  R3 = Resistor [tolerance=±5% resistance=220 package=THT]
  R4 = Resistor [tolerance=±5% resistance=220 package=THT]

nets:
  N1: Raspberry_Pi_1.GND, S1.Pin_1, S1.Pin_2, LED1.common_cathode
  N2: Raspberry_Pi_1.GIPO20, R4.Pin_0
  N3: Raspberry_Pi_1.GIPO16, R3.Pin_0
  N4: Raspberry_Pi_1.GIPO12, R2.Pin_0
  N5: Raspberry_Pi_1.GIPO25, S1.Pin_3, S1.Pin_4, R1.Pin_1
  N6: LED1.red_anode, R2.Pin_1
  N7: LED1.green_anode, R3.Pin_1
  N8: LED1.blue_anode, R4.Pin_1

notes:
  Raspberry Pi 3 B+
  Button GPIO 25
  Common cathode RGB LED
  First lead: RED, GPIO 12
  Second lead: CATHODE, GND
  Third lead: GREEN, GPIO 16
  Fourth lead: BLUE, GPIO 20
