# Fritzing sketch midi_light_show (saved by Fritzing 0.9.3b)
breadboards: 1

parts:
  Raspberry_Pi_1 = Raspberry Pi 3 [part_number=RPI-3-V1.2]
  LED2 = LED - 5mm [color="Red (633nm)" package="5 mm [THT]"]
  LED3 = LED - 5mm [color="Green (565nm)" package="5 mm [THT]"]
  LED4 = LED - 5mm [color="Blue (430nm)" package="5 mm [THT]"]
  LED5 = LED - 5mm [color="Yellow (595nm)" package="5 mm [THT]"]
  LED6 = LED - 5mm [color="Red (633nm)" package="5 mm [THT]"]
  LED7 = LED - 5mm [color="Green (565nm)" package="5 mm [THT]"]
  LED8 = LED - 5mm [color="Blue (430nm)" package="5 mm [THT]"]
  LED9 = LED - 5mm [color="Yellow (595nm)" package="5 mm [THT]"]
  R5 = Resistor [tolerance=±5% resistance=220 package=THT]
  R6 = Resistor [tolerance=±5% resistance=220 package=THT]
  R7 = Resistor [tolerance=±5% resistance=220 package=THT]
  R8 = Resistor [tolerance=±5% resistance=220 package=THT]
  R9 = Resistor [tolerance=±5% resistance=220 package=THT]
  R10 = Resistor [tolerance=±5% resistance=220 package=THT]
  R11 = Resistor [tolerance=±5% resistance=220 package=THT]
  R12 = Resistor [tolerance=±5% resistance=220 package=THT]

nets:
  N1: Raspberry_Pi_1.GIPO5, LED4.anode
  N2: Raspberry_Pi_1.GIPO6, LED3.anode
  N3: Raspberry_Pi_1.GIPO13, LED2.anode
  N4: Raspberry_Pi_1.GND, R7.Pin_0, R8.Pin_0, R9.Pin_0, R11.Pin_0
  N5: Raspberry_Pi_1.GIPO7, LED5.anode
  N6: Raspberry_Pi_1.GIPO23, LED6.anode
  N7: Raspberry_Pi_1.GIPO18, LED7.anode
  N8: Raspberry_Pi_1.GIPO15, LED8.anode
  N9: Raspberry_Pi_1.GIPO14, LED9.anode
  N10: LED2.cathode, R8.Pin_1
  N11: LED3.cathode, R6.Pin_1
  N12: LED4.cathode, R7.Pin_1
  N13: LED5.cathode, R5.Pin_1
  N14: LED6.cathode, R9.Pin_1
  N15: LED7.cathode, R10.Pin_1
  N16: LED8.cathode, R11.Pin_1
  N17: LED9.cathode, R12.Pin_1

notes:
  Raspberry Pi 3 B+
  LEDs:
  RED, GPIO 13
  GREEN, GPIO 06
  BLUE, GPIO 05
  YELLOW, GPIO 07
  RED, GPIO 23
  GREEN, GPIO 18
  BLUE, GPIO 15
  YELLOW, GPIO 14
